# Fritzing sketch ESP8266_only (saved by Fritzing 0.9.2b)
breadboards: 2

parts:
  Part1 = Arduino Uno (Rev3) - ICSP
  U1 = ESP8266 WiFi Module [part_number=ESP8266]
  Part2 = Arduino Uno (Rev3) - ICSP
  U2 = ESP8266 WiFi Module [part_number=ESP8266]
  DHT1 = DHT11 Humitidy and Temperature Sensor

nets:
  N1: Part1.D5_PWM, U1.TXD
  N2: Part1.D7, U1.RXD
  GND: Part1.GND, U1.GND
  N3: Part2.D4, DHT1.DATA
  N4: Part2.D5_PWM, U2.TXD
  N5: Part2.D7, U2.RXD
  GND_2: Part2.GND, U2.GND, DHT1.GND
  N6: U2.CH_PD, DHT1.VDD

custom parts:
  ESP8266 WiFi Module: Generic WiFi Module based on the ESP8266 with onboard PCB antenna and UART communications
  DHT11 Humitidy and Temperature Sensor: DHT11 Humidity and Temperature Sensor
